// Digital circuit 4to1MUX.dig as structural Verilog
module _4to1MUX (
  input  Sel1,
  input  Sel0,
  input  X0,
  input  X1,
  input  X2,
  input  X3,
  output Rez
);

  wire and_1_out, and_2_out, and_3_out, and_4_out, not_1_out, not_2_out;

  not not_1 (not_1_out, Sel1);
  not not_2 (not_2_out, Sel0);
  and and_1 (and_1_out, not_2_out, not_1_out, X0);
  and and_2 (and_2_out, Sel0, not_1_out, X1);
  and and_3 (and_3_out, not_2_out, Sel1, X2);
  and and_4 (and_4_out, Sel0, Sel1, X3);
  or or_1 (Rez, and_1_out, and_2_out, and_3_out, and_4_out);
endmodule
