// Logisim project Alu.circ as structural Verilog
module adunare (
  input  [15:0] INBUS,
  input  Start,
  input  RST,
  output Stop,
  output [7:0] OUTBUS
);

  wire clock_1_out, control_unit_1_c0, control_unit_1_c1, control_unit_1_c2, control_unit_1_c3,
       controlled_buffer_2_out, controlled_buffer_4_out;
  wire [7:0] controlled_buffer_3_out, controlled_buffer_5_out, parallel_adder_1_z, register_1_q, register_2_q;

  Clock clock_1 (.out(clock_1_out));
  assign OUTBUS = control_unit_1_c1 ? parallel_adder_1_z : 8'bz;  // Controlled_Buffer controlled_buffer_1
  assign controlled_buffer_2_out = control_unit_1_c3 ? clock_1_out : 1'bz;  // Controlled_Buffer controlled_buffer_2
  assign controlled_buffer_3_out = control_unit_1_c3 ? INBUS[15:8] : 8'bz;  // Controlled_Buffer controlled_buffer_3
  Register register_1 (
    .D(controlled_buffer_3_out), .en(1'b1), .clk(controlled_buffer_2_out), .Q(register_1_q));  // open: clr
  assign controlled_buffer_4_out = control_unit_1_c2 ? clock_1_out : 1'bz;  // Controlled_Buffer controlled_buffer_4
  assign controlled_buffer_5_out = control_unit_1_c2 ? INBUS[7:0] : 8'bz;  // Controlled_Buffer controlled_buffer_5
  Register register_2 (
    .D(controlled_buffer_5_out), .en(1'b1), .clk(controlled_buffer_4_out), .Q(register_2_q));  // open: clr
  Parallel_Adder parallel_adder_1 (.x(register_1_q), .y(register_2_q), .z(parallel_adder_1_z), .c_in(1'b0));
  Control_Unit control_unit_1 (
    .S(Start), .Q0(clock_1_out), .Q_1(RST), .RST(control_unit_1_c1), .c0(control_unit_1_c0),
    .c1(control_unit_1_c1), .c2(control_unit_1_c2), .c3(control_unit_1_c3), .c4(Stop), .c7(control_unit_1_c1));  // open: CNT7, Beg, Sel, CLK, c5, c6, c8, Sf, c9, c10, c11, c12
endmodule

module FAC (
  input  xi,
  input  yi,
  input  ci,
  output ci_out,
  output zi
);

  wire and_1_out, and_2_out, and_3_out, xor_1_out;

  or or_1 (ci_out, and_1_out, and_2_out, and_3_out);
  and and_1 (and_1_out, xi, ci);
  and and_2 (and_2_out, ci, yi);
  and and_3 (and_3_out, xi, yi);
  xor xor_1 (xor_1_out, xi, yi);
  xor xor_2 (zi, xor_1_out, ci);
endmodule

module RCA_4 (
  input  [3:0] x,
  input  [3:0] y,
  input  c_in,
  output c_out,
  output [3:0] z
);

  wire fac_2_ci_out, fac_3_ci_out, fac_4_ci_out;

  FAC fac_1 (.ci_out(c_out), .xi(x[3]), .yi(y[3]), .zi(z[3]), .ci(fac_2_ci_out));
  FAC fac_2 (.ci_out(fac_2_ci_out), .xi(x[2]), .yi(y[2]), .zi(z[2]), .ci(fac_3_ci_out));
  FAC fac_3 (.ci_out(fac_3_ci_out), .xi(x[1]), .yi(y[1]), .zi(z[1]), .ci(fac_4_ci_out));
  FAC fac_4 (.ci_out(fac_4_ci_out), .xi(x[0]), .yi(y[0]), .zi(z[0]), .ci(c_in));
endmodule

module Parallel_Adder (
  input  [7:0] x,
  input  [7:0] y,
  input  c_in,
  output [7:0] z
);

  wire rca_4_2_c_out;

  RCA_4 rca_4_1 (.x(x[7:4]), .y(y[7:4]), .z(z[7:4]), .c_in(rca_4_2_c_out));  // open: c_out
  RCA_4 rca_4_2 (.c_out(rca_4_2_c_out), .x(x[3:0]), .y(y[3:0]), .z(z[3:0]), .c_in(c_in));
endmodule

module Control_Unit (
  input  S,
  input  Q0,
  input  Q_1,
  input  CNT7,
  input  Beg,
  input  [1:0] Sel,
  input  CLK,
  input  RST,
  output c0,
  output c1,
  output c2,
  output c3,
  output c4,
  output c5,
  output c6,
  output c7,
  output c8,
  output Sf,
  output c9,
  output c10,
  output c11,
  output c12
);

  wire and_1_out, and_2_out, and_3_out, and_4_out, and_5_out, and_6_out, and_7_out, and_8_out, and_9_out,
       and_10_out, and_11_out, and_12_out, and_13_out, and_14_out, and_15_out, and_16_out, and_17_out,
       and_18_out, and_19_out, and_20_out, and_21_out, and_22_out, and_23_out, B5_q, not_1_out, not_2_out,
       not_3_out, not_4_out, not_5_out, not_6_out, not_7_out, not_8_out, not_9_out, not_10_out, not_11_out,
       not_12_out, not_13_out, not_14_out, or_1_out, or_2_out, or_3_out, or_4_out, or_5_out, or_6_out,
       or_7_out, or_8_out, or_9_out, or_10_out, xnor_1_out;

  not not_1 (not_1_out, Sel[1]);
  and and_1 (and_1_out, not_1_out, or_1_out);
  and and_2 (and_2_out, Sel[1], c11);
  D_Flip_Flop B13 (.D(and_2_out), .clk(CLK), .Q(c12), .reset(RST));  // open: Qn, preset
  not not_2 (not_2_out, S);
  or or_1 (or_1_out, c5, B5_q);
  and and_3 (and_3_out, not_2_out, CNT7, c8);
  or or_2 (or_2_out, and_1_out, c10, and_3_out, and_4_out);
  D_Flip_Flop B12 (.D(or_2_out), .clk(CLK), .Q(c11), .reset(RST));  // open: Qn, preset
  and and_4 (and_4_out, CNT7, c9);
  and and_5 (and_5_out, S, CNT7, c8);
  D_Flip_Flop B11 (.D(and_5_out), .clk(CLK), .Q(c10), .reset(RST));  // open: Qn, preset
  D_Flip_Flop B10 (.D(c7), .clk(CLK), .Q(c9), .reset(RST));  // open: Qn, preset
  xnor xnor_1 (xnor_1_out, Q0, Q_1);
  and and_6 (and_6_out, xnor_1_out, c3, Sel[1], not_4_out, not_3_out);
  D_Flip_Flop B9 (.D(c6), .clk(CLK), .Q(c8), .reset(RST));  // open: Qn, preset
  not not_3 (not_3_out, CNT7);
  not not_4 (not_4_out, Sel[0]);
  and and_7 (and_7_out, Sel[1], not_4_out, or_4_out);
  or or_3 (or_3_out, and_6_out, and_7_out);
  D_Flip_Flop B8 (.D(or_3_out), .clk(CLK), .Q(c7), .reset(RST));  // open: Qn, preset
  or or_4 (or_4_out, c5, B5_q);
  and and_8 (and_8_out, or_4_out, Sel[0], Sel[1]);
  D_Flip_Flop B7 (.D(and_8_out), .clk(CLK), .Q(c6), .reset(RST));  // open: Qn, preset
  and and_9 (and_9_out, Sel[0], not_6_out);
  and and_10 (and_10_out, c3, or_6_out);
  not not_5 (not_5_out, S);
  and and_11 (and_11_out, not_5_out, Sel[0], Sel[1]);
  not not_6 (not_6_out, Sel[1]);
  or or_5 (or_5_out, and_11_out, and_13_out);
  and and_12 (and_12_out, not_3_out, or_5_out);
  or or_6 (or_6_out, and_9_out, and_12_out);
  D_Flip_Flop B6 (.D(and_10_out), .clk(CLK), .Q(c5), .reset(RST));  // open: Qn, preset
  not not_7 (not_7_out, Q_1);
  not not_8 (not_8_out, Sel[0]);
  and and_13 (and_13_out, Sel[1], not_8_out, Q0, not_7_out);
  not not_9 (not_9_out, Sel[1]);
  and and_14 (and_14_out, not_9_out, not_8_out);
  or or_7 (or_7_out, and_14_out, and_17_out);
  and and_15 (and_15_out, c3, or_7_out);
  D_Flip_Flop B5 (.D(and_15_out), .clk(CLK), .Q(B5_q), .reset(RST));  // open: Qn, preset
  and and_16 (and_16_out, Sel[1], Sel[0], S);
  or or_8 (or_8_out, and_16_out, and_18_out);
  and and_17 (and_17_out, not_3_out, or_8_out);
  or or_9 (or_9_out, c2, c1, c0);
  D_Flip_Flop B4 (.D(or_9_out), .clk(CLK), .Q(c3), .reset(RST));  // open: Qn, preset
  not not_10 (not_10_out, Q0);
  not not_11 (not_11_out, Sel[0]);
  and and_18 (and_18_out, not_11_out, Sel[1], not_10_out, Q_1);
  and and_19 (and_19_out, Sel[1], Sel[0], Beg, Sf);
  D_Flip_Flop B3 (.D(and_19_out), .clk(CLK), .Q(c2), .reset(RST));  // open: Qn, preset
  not not_12 (not_12_out, Sel[0]);
  and and_20 (and_20_out, Sel[1], not_12_out, Beg, Sf);
  D_Flip_Flop B2 (.D(and_20_out), .clk(CLK), .Q(c1), .reset(RST));  // open: Qn, preset
  not not_13 (not_13_out, Sel[1]);
  and and_21 (and_21_out, not_13_out, Beg, Sf);
  D_Flip_Flop B1 (.D(and_21_out), .clk(CLK), .Q(c0), .reset(RST));  // open: Qn, preset
  not not_14 (not_14_out, Beg);
  and and_22 (and_22_out, Sf, not_14_out);
  and and_23 (and_23_out, not_13_out, c11);
  or or_10 (or_10_out, and_22_out, and_23_out, c12);
  D_Flip_Flop B0 (.D(or_10_out), .clk(CLK), .Q(Sf), .reset(RST));  // open: Qn, preset
  or or_11 (c4, B5_q, c5);
endmodule

module UShift (
  input  BitShiftRight,
  input  A7,
  input  A6,
  input  A5,
  input  A4,
  input  A3,
  input  A2,
  input  A1,
  input  A0,
  input  BitShiftLeft,
  input  Reset,
  input  [1:0] Selector,
  input  CLK,
  output out_14,
  output out_15,
  output out_16,
  output out_17,
  output out_18,
  output out_19,
  output out_20,
  output out_21
);

  wire multiplexer_1_out, multiplexer_2_out, multiplexer_3_out, multiplexer_4_out, multiplexer_5_out,
       multiplexer_6_out, multiplexer_7_out, multiplexer_8_out;

  Multiplexer #(.select(2)) multiplexer_1 (
    .in0(out_20), .in1(out_19), .in2(out_21), .in3(A1), .out(multiplexer_1_out), .sel(Selector));
  Multiplexer #(.select(2)) multiplexer_2 (
    .in0(out_21), .in1(out_20), .in2(BitShiftLeft), .in3(A0), .out(multiplexer_2_out), .sel(Selector));
  Multiplexer #(.select(2)) multiplexer_3 (
    .in0(out_14), .in1(BitShiftRight), .in2(out_15), .in3(A7), .out(multiplexer_3_out), .sel(Selector));
  Multiplexer #(.select(2)) multiplexer_4 (
    .in0(out_15), .in1(out_14), .in2(out_16), .in3(A6), .out(multiplexer_4_out), .sel(Selector));
  Multiplexer #(.select(2)) multiplexer_5 (
    .in0(out_16), .in1(out_15), .in2(out_17), .in3(A5), .out(multiplexer_5_out), .sel(Selector));
  Multiplexer #(.select(2)) multiplexer_6 (
    .in0(out_17), .in1(out_16), .in2(out_18), .in3(A4), .out(multiplexer_6_out), .sel(Selector));
  Multiplexer #(.select(2)) multiplexer_7 (
    .in0(out_18), .in1(out_17), .in2(out_19), .in3(A3), .out(multiplexer_7_out), .sel(Selector));
  Multiplexer #(.select(2)) multiplexer_8 (
    .in0(out_19), .in1(out_18), .in2(out_20), .in3(A2), .out(multiplexer_8_out), .sel(Selector));
  D_Flip_Flop d_ff_1 (.D(multiplexer_3_out), .clk(CLK), .Q(out_14), .reset(Reset));  // open: Qn, preset
  D_Flip_Flop d_ff_2 (.D(multiplexer_4_out), .clk(CLK), .Q(out_15), .reset(Reset));  // open: Qn, preset
  D_Flip_Flop d_ff_3 (.D(multiplexer_5_out), .clk(CLK), .Q(out_16), .reset(Reset));  // open: Qn, preset
  D_Flip_Flop d_ff_4 (.D(multiplexer_6_out), .clk(CLK), .Q(out_17), .reset(Reset));  // open: Qn, preset
  D_Flip_Flop d_ff_5 (.D(multiplexer_7_out), .clk(CLK), .Q(out_18), .reset(Reset));  // open: Qn, preset
  D_Flip_Flop d_ff_6 (.D(multiplexer_8_out), .clk(CLK), .Q(out_19), .reset(Reset));  // open: Qn, preset
  D_Flip_Flop d_ff_7 (.D(multiplexer_1_out), .clk(CLK), .Q(out_20), .reset(Reset));  // open: Qn, preset
  D_Flip_Flop d_ff_8 (.D(multiplexer_2_out), .clk(CLK), .Q(out_21), .reset(Reset));  // open: Qn, preset

  // Notes on the sheet:
  //   Selector: 00(nu face nimic); 11(load); 01(shift dreapta); 10(shift stanga)
endmodule

module CNT (
  input  M,
  input  CLK,
  input  RST,
  output CNT7
);

  wire and_1_out, and_2_out, T0_q, T1_q, T2_q;

  and and_1 (and_1_out, M, T0_q, T1_q);
  T_Flip_Flop T2 (.T(and_1_out), .clk(CLK), .Q(T2_q), .reset(RST));  // open: Qn, preset
  and and_2 (and_2_out, M, T0_q);
  T_Flip_Flop T1 (.T(and_2_out), .clk(CLK), .Q(T1_q), .reset(RST));  // open: Qn, preset
  and and_3 (CNT7, T2_q, T1_q, T0_q);
  T_Flip_Flop T0 (.T(M), .clk(CLK), .Q(T0_q), .reset(RST));  // open: Qn, preset
endmodule

module Cunit (
  input  SIGN,
  input  Q0,
  input  Q_1,
  input  CNT7,
  input  [1:0] SEL,
  input  RST,
  input  BGN,
  output c0,
  output c1,
  output c2,
  output c3,
  output c4,
  output c5,
  output c6,
  output c7,
  output c8,
  output c9,
  output c10,
  output c11,
  output c12,
  output c13,
  output c14,
  output SF
);

  wire and_1_out, and_2_out, and_3_out, and_4_out, and_5_out, and_6_out, and_7_out, and_8_out, and_9_out,
       and_10_out, and_11_out, and_12_out, and_13_out, and_14_out, and_15_out, and_16_out, and_17_out,
       and_18_out, and_19_out, and_20_out, and_21_out, and_22_out, and_23_out, and_24_out, and_25_out,
       and_26_out, and_27_out, and_28_out, and_29_out, B5_q, bo_negbgn_out, CLK_out, not_1_out, not_2_out,
       not_3_out, not_4_out, not_5_out, not_6_out, not_7_out, not_8_out, not_9_out, not_10_out, not_11_out,
       not_12_out, not_13_out, or_1_out, or_2_out, or_3_out, or_4_out, or_5_out, or_6_out, or_7_out,
       or_8_out, or_9_out, xnor_1_out;

  Clock CLK (.out(CLK_out));
  not not_1 (not_1_out, SEL[0]);
  not not_2 (not_2_out, SEL[1]);
  D_Flip_Flop B15 (.D(and_1_out), .clk(CLK_out), .Q(c14), .reset(RST));  // open: Qn, preset
  and and_1 (and_1_out, c12, SEL[1], SEL[0]);
  D_Flip_Flop B14 (.D(and_2_out), .clk(CLK_out), .Q(c13), .reset(RST));  // open: Qn, preset
  and and_2 (and_2_out, c10, CNT7);
  not not_3 (not_3_out, SIGN);
  and and_3 (and_3_out, c9, CNT7, not_3_out);
  or or_1 (or_1_out, and_3_out, c11, and_4_out);
  and and_4 (and_4_out, not_2_out, or_4_out);
  D_Flip_Flop B13 (.D(or_1_out), .clk(CLK_out), .Q(c12), .reset(RST));  // open: Qn, preset
  and and_5 (and_5_out, c9, CNT7, SIGN);
  D_Flip_Flop B12 (.D(and_5_out), .clk(CLK_out), .Q(c11), .reset(RST));  // open: Qn, preset
  not not_4 (not_4_out, CNT7);
  and and_6 (and_6_out, not_4_out, and_10_out, c10);
  D_Flip_Flop B11 (.D(c8), .clk(CLK_out), .Q(c10), .reset(RST));  // open: Qn, preset
  xnor xnor_1 (xnor_1_out, Q0, Q_1);
  and and_7 (and_7_out, and_6_out, xnor_1_out);
  and and_8 (and_8_out, xnor_1_out, and_9_out);
  and and_9 (and_9_out, c3, and_10_out);
  and and_10 (and_10_out, SEL[1], not_1_out);
  D_Flip_Flop B10 (.D(c7), .clk(CLK_out), .Q(c9), .reset(RST));  // open: Qn, preset
  and and_11 (and_11_out, not_2_out, SEL[0]);
  and and_12 (and_12_out, and_10_out, or_4_out);
  or or_2 (or_2_out, and_7_out, and_8_out, and_12_out);
  not not_5 (not_5_out, SIGN);
  and and_13 (and_13_out, SEL[0], SEL[1], not_5_out);
  or or_3 (or_3_out, and_11_out, and_13_out, and_15_out);
  and and_14 (and_14_out, c3, or_3_out);
  D_Flip_Flop B9 (.D(or_2_out), .clk(CLK_out), .Q(c8), .reset(RST));  // open: Qn, preset
  not not_6 (not_6_out, Q_1);
  and and_15 (and_15_out, SEL[1], not_1_out, Q0, not_6_out);
  not not_7 (not_7_out, Q_1);
  not not_8 (not_8_out, not_10_out);
  and and_16 (and_16_out, c10, SEL[1], not_1_out, not_8_out, not_7_out, not_11_out);
  D_Flip_Flop B8 (.D(c6), .clk(CLK_out), .Q(c7), .reset(RST));  // open: Qn, preset
  not not_9 (not_9_out, SIGN);
  and and_17 (and_17_out, c9, not_11_out, SEL[1], SEL[0], not_9_out);
  D_Flip_Flop B7 (.D(and_18_out), .clk(CLK_out), .Q(c6), .reset(RST));  // open: Qn, preset
  and and_18 (and_18_out, SEL[0], SEL[1], or_4_out);
  or or_4 (or_4_out, c5, B5_q);
  and and_19 (and_19_out, not_2_out, not_1_out);
  D_Flip_Flop B6 (.D(or_5_out), .clk(CLK_out), .Q(c5), .reset(RST));  // open: Qn, preset
  or or_5 (or_5_out, and_14_out, and_16_out, and_17_out);
  not not_10 (not_10_out, Q0);
  and and_20 (and_20_out, SEL[0], SEL[1], SIGN);
  or or_6 (or_6_out, and_19_out, and_20_out, and_22_out);
  and and_21 (and_21_out, c3, or_6_out);
  or or_7 (or_7_out, and_21_out, and_23_out, and_24_out);
  and and_22 (and_22_out, not_10_out, SEL[1], Q_1, not_1_out);
  D_Flip_Flop B5 (.D(or_7_out), .clk(CLK_out), .Q(B5_q), .reset(RST));  // open: Qn, preset
  or or_8 (or_8_out, c2, c0, c1);
  not not_11 (not_11_out, CNT7);
  and and_23 (and_23_out, c10, SEL[1], not_1_out, not_10_out, Q_1, not_11_out);
  D_Flip_Flop B4 (.D(or_8_out), .clk(CLK_out), .Q(c3), .reset(RST));  // open: Qn, preset
  and and_24 (and_24_out, c9, not_11_out, SEL[1], SEL[0], SIGN);
  not not_12 (not_12_out, not_1_out);
  D_Flip_Flop B3 (.D(and_25_out), .clk(CLK_out), .Q(c2), .reset(RST));  // open: Qn, preset
  and and_25 (and_25_out, not_12_out, and_26_out);
  and and_26 (and_26_out, SEL[1], SF, BGN);
  D_Flip_Flop B2 (.D(and_27_out), .clk(CLK_out), .Q(c1), .reset(RST));  // open: Qn, preset
  and and_27 (and_27_out, and_26_out, not_1_out);
  and and_28 (and_28_out, not_2_out, BGN, SF);
  D_Flip_Flop B1 (.D(and_28_out), .clk(CLK_out), .Q(c0), .reset(RST));  // open: Qn, preset
  and and_29 (and_29_out, c12, not_2_out);
  or or_9 (or_9_out, and_29_out, c14, c13, bo_negbgn_out);
  not not_13 (not_13_out, BGN);
  and bo_negbgn (bo_negbgn_out, SF, not_13_out);
  D_Flip_Flop B0 (.D(or_9_out), .clk(CLK_out), .Q(SF), .reset(RST));  // open: Qn, preset
  or or_10 (c4, B5_q, c5);
endmodule
