// Digital circuit FAC.dig as structural Verilog
module FAC (
  input  A,
  input  B,
  input  CarryIn,
  output Z,
  output CarryOut
);

  wire and_1_out, and_2_out, and_3_out, xor_1_out;

  xor xor_1 (xor_1_out, A, B);
  and and_1 (and_1_out, A, B);
  and and_2 (and_2_out, B, CarryIn);
  and and_3 (and_3_out, A, CarryIn);
  xor xor_2 (Z, xor_1_out, CarryIn);
  or or_1 (CarryOut, and_1_out, and_2_out, and_3_out);
endmodule
