// Logisim project UShiftReg.circ as structural Verilog: 6 circuits, main circuit adunare
module adunare (
  input  [15:0] INBUS,
  input  Start,
  input  RST,
  output Stop,
  output [7:0] OUTBUS
);

  wire clock_1_out, control_unit_1_c0, control_unit_1_c1, control_unit_1_c2, control_unit_1_c3,
       controlled_buffer_2_out, controlled_buffer_4_out;
  wire [7:0] controlled_buffer_3_out, controlled_buffer_5_out, parallel_adder_1_z, register_1_q, register_2_q;

  Clock clock_1 (.out(clock_1_out));
  assign OUTBUS = control_unit_1_c2 ? parallel_adder_1_z : 8'bz;  // Controlled_Buffer controlled_buffer_1
  assign controlled_buffer_2_out = control_unit_1_c0 ? clock_1_out : 1'bz;  // Controlled_Buffer controlled_buffer_2
  assign controlled_buffer_3_out = control_unit_1_c0 ? INBUS[15:8] : 8'bz;  // Controlled_Buffer controlled_buffer_3
  Register register_1 (
    .D(controlled_buffer_3_out), .en(1'b1), .clk(controlled_buffer_2_out), .Q(register_1_q));  // open: clr
  assign controlled_buffer_4_out = control_unit_1_c1 ? clock_1_out : 1'bz;  // Controlled_Buffer controlled_buffer_4
  assign controlled_buffer_5_out = control_unit_1_c1 ? INBUS[7:0] : 8'bz;  // Controlled_Buffer controlled_buffer_5
  Register register_2 (
    .D(controlled_buffer_5_out), .en(1'b1), .clk(controlled_buffer_4_out), .Q(register_2_q));  // open: clr
  Parallel_Adder parallel_adder_1 (.x(register_1_q), .y(register_2_q), .z(parallel_adder_1_z), .c_in(1'b0));
  Control_Unit control_unit_1 (
    .Start(Start), .CLK(clock_1_out), .RST(RST), .c3(control_unit_1_c3), .c2(control_unit_1_c2),
    .c1(control_unit_1_c1), .c0(control_unit_1_c0), .Stop(Stop));

  // Notes on the sheet:
  //   Ca sa putem folosi si aici c3 ar trebui sa avem registru si pentru output dar nu l-am facut doar pentru adunare
endmodule

module FAC (
  input  xi,
  input  yi,
  input  ci,
  output ci_out,
  output zi
);

  wire and_1_out, and_2_out, and_3_out, xor_1_out;

  or or_1 (ci_out, and_1_out, and_2_out, and_3_out);
  and and_1 (and_1_out, xi, ci);
  and and_2 (and_2_out, ci, yi);
  and and_3 (and_3_out, xi, yi);
  xor xor_1 (xor_1_out, xi, yi);
  xor xor_2 (zi, xor_1_out, ci);
endmodule

module RCA_4 (
  input  [3:0] x,
  input  [3:0] y,
  input  c_in,
  output c_out,
  output [3:0] z
);

  wire fac_2_ci_out, fac_3_ci_out, fac_4_ci_out;

  FAC fac_1 (.ci_out(c_out), .xi(x[3]), .yi(y[3]), .zi(z[3]), .ci(fac_2_ci_out));
  FAC fac_2 (.ci_out(fac_2_ci_out), .xi(x[2]), .yi(y[2]), .zi(z[2]), .ci(fac_3_ci_out));
  FAC fac_3 (.ci_out(fac_3_ci_out), .xi(x[1]), .yi(y[1]), .zi(z[1]), .ci(fac_4_ci_out));
  FAC fac_4 (.ci_out(fac_4_ci_out), .xi(x[0]), .yi(y[0]), .zi(z[0]), .ci(c_in));
endmodule

module Parallel_Adder (
  input  [7:0] x,
  input  [7:0] y,
  input  c_in,
  output [7:0] z
);

  wire rca_4_2_c_out;

  RCA_4 rca_4_1 (.x(x[7:4]), .y(y[7:4]), .z(z[7:4]), .c_in(rca_4_2_c_out));  // open: c_out
  RCA_4 rca_4_2 (.c_out(rca_4_2_c_out), .x(x[3:0]), .y(y[3:0]), .z(z[3:0]), .c_in(c_in));
endmodule

module Control_Unit (
  input  Start,
  input  CLK,
  input  RST,
  output c3,
  output c2,
  output c1,
  output c0,
  output Stop
);

  wire and_1_out, and_2_out, not_1_out, or_1_out;

  D_Flip_Flop B4 (.D(c2), .clk(CLK), .Q(c3), .reset(RST));  // open: Qn, preset
  D_Flip_Flop B3 (.D(c1), .clk(CLK), .Q(c2), .reset(RST));  // open: Qn, preset
  D_Flip_Flop B2 (.D(c0), .clk(CLK), .Q(c1), .reset(RST));  // open: Qn, preset
  and and_1 (and_1_out, Start, Stop);
  D_Flip_Flop B1 (.D(and_1_out), .clk(CLK), .Q(c0), .reset(RST));  // open: Qn, preset
  not not_1 (not_1_out, Start);
  and and_2 (and_2_out, not_1_out, Stop);
  or or_1 (or_1_out, and_2_out, c3);
  D_Flip_Flop B0 (.D(or_1_out), .clk(CLK), .Q(Stop), .preset(RST));  // open: Qn, reset

  // Notes on the sheet:
  //   Start e Begin
  //   Stop e END
endmodule

module UShift (
  input  BitShiftRight,
  input  A7,
  input  A6,
  input  A5,
  input  A4,
  input  A3,
  input  A2,
  input  A1,
  input  BitShiftLeft,
  input  A0,
  input  Reset,
  input  [1:0] Selector,
  output out_13,
  output out_14,
  output out_15,
  output out_16,
  output out_17,
  output out_18,
  output out_19,
  output out_20
);

  wire Cloci_out, multiplexer_1_out, multiplexer_2_out, multiplexer_3_out, multiplexer_4_out,
       multiplexer_5_out, multiplexer_6_out, multiplexer_7_out, multiplexer_8_out;

  Multiplexer #(.select(2)) multiplexer_1 (
    .in0(out_19), .in1(out_18), .in2(out_20), .in3(A1), .out(multiplexer_1_out), .sel(Selector));
  Multiplexer #(.select(2)) multiplexer_2 (
    .in0(out_20), .in1(out_19), .in2(BitShiftLeft), .in3(A0), .out(multiplexer_2_out), .sel(Selector));
  Multiplexer #(.select(2)) multiplexer_3 (
    .in0(out_13), .in1(BitShiftRight), .in2(out_14), .in3(A7), .out(multiplexer_3_out), .sel(Selector));
  Multiplexer #(.select(2)) multiplexer_4 (
    .in0(out_14), .in1(out_13), .in2(out_15), .in3(A6), .out(multiplexer_4_out), .sel(Selector));
  Multiplexer #(.select(2)) multiplexer_5 (
    .in0(out_15), .in1(out_14), .in2(out_16), .in3(A5), .out(multiplexer_5_out), .sel(Selector));
  Multiplexer #(.select(2)) multiplexer_6 (
    .in0(out_16), .in1(out_15), .in2(out_17), .in3(A4), .out(multiplexer_6_out), .sel(Selector));
  Multiplexer #(.select(2)) multiplexer_7 (
    .in0(out_17), .in1(out_16), .in2(out_18), .in3(A3), .out(multiplexer_7_out), .sel(Selector));
  Multiplexer #(.select(2)) multiplexer_8 (
    .in0(out_18), .in1(out_17), .in2(out_19), .in3(A2), .out(multiplexer_8_out), .sel(Selector));
  Clock Cloci (.out(Cloci_out));
  D_Flip_Flop d_ff_1 (.D(multiplexer_3_out), .clk(Cloci_out), .Q(out_13), .reset(Reset));  // open: Qn, preset
  D_Flip_Flop d_ff_2 (.D(multiplexer_4_out), .clk(Cloci_out), .Q(out_14), .reset(Reset));  // open: Qn, preset
  D_Flip_Flop d_ff_3 (.D(multiplexer_5_out), .clk(Cloci_out), .Q(out_15), .reset(Reset));  // open: Qn, preset
  D_Flip_Flop d_ff_4 (.D(multiplexer_6_out), .clk(Cloci_out), .Q(out_16), .reset(Reset));  // open: Qn, preset
  D_Flip_Flop d_ff_5 (.D(multiplexer_7_out), .clk(Cloci_out), .Q(out_17), .reset(Reset));  // open: Qn, preset
  D_Flip_Flop d_ff_6 (.D(multiplexer_8_out), .clk(Cloci_out), .Q(out_18), .reset(Reset));  // open: Qn, preset
  D_Flip_Flop d_ff_7 (.D(multiplexer_1_out), .clk(Cloci_out), .Q(out_19), .reset(Reset));  // open: Qn, preset
  D_Flip_Flop d_ff_8 (.D(multiplexer_2_out), .clk(Cloci_out), .Q(out_20), .reset(Reset));  // open: Qn, preset
endmodule
