// Logisim project shiftregister.circ as structural Verilog: 2 circuits, main circuit main
// A0
module main (
  input  ShiftRight,
  input  a3,
  input  a2,
  input  a1,
  input  ShiftLeft,
  input  a0,
  input  [1:0] in_7,
  output a3shift,
  output a2shift,
  output a1shift,
  output a0shift
);

  wire button_1_out, clcok_out, d_ff_1_qn, multiplexer_1_out, multiplexer_2_out, multiplexer_3_out,
       multiplexer_4_out, undriven, undriven_2;

  Multiplexer #(.enable("true"), .select(2)) multiplexer_1 (
    .in0(a3shift), .in1(ShiftRight), .in2(undriven), .in3(a3), .out(multiplexer_1_out), .sel(in_7));  // open: en
  Multiplexer #(.enable("true"), .select(2)) multiplexer_2 (
    .in0(undriven), .in1(a3shift), .in2(undriven_2), .in3(a2), .out(multiplexer_2_out), .sel(in_7));  // open: en
  Multiplexer #(.enable("true"), .select(2)) multiplexer_3 (
    .in0(undriven_2), .in1(a2shift), .in2(a0shift), .in3(a1), .out(multiplexer_3_out), .sel(in_7));  // open: en
  Multiplexer #(.enable("true"), .select(2)) multiplexer_4 (
    .in0(a0shift), .in1(a1shift), .in2(ShiftLeft), .in3(a0), .out(multiplexer_4_out), .sel(in_7));  // open: en
  Clock clcok (.out(clcok_out));
  D_Flip_Flop d_ff_1 (
    .D(multiplexer_1_out), .clk(clcok_out), .Q(a3shift), .Qn(d_ff_1_qn), .reset(button_1_out));  // open: preset
  D_Flip_Flop d_ff_2 (.D(multiplexer_2_out), .clk(clcok_out), .Q(a2shift), .reset(button_1_out));  // open: Qn, preset
  D_Flip_Flop d_ff_3 (.D(multiplexer_3_out), .clk(clcok_out), .Q(a1shift), .reset(button_1_out));  // open: Qn, preset
  D_Flip_Flop d_ff_4 (.D(multiplexer_4_out), .clk(clcok_out), .Q(a0shift), .reset(button_1_out));  // open: Qn, preset
  Button button_1 (.out(button_1_out));
endmodule

module dfg (
);

  main main_1 ();  // open: ShiftRight, a3, a2, a1, ShiftLeft, a0, in_7, a3shift, a2shift, a1shift, a0shift
endmodule
