// Logisim project try.circ as structural Verilog: 2 circuits, main circuit main
module main (
  input  ci,
  input  xi,
  input  yi,
  output zi,
  output ci_out
);

  wire and_1_out, and_2_out, and_3_out, xor_2_out;

  or or_1 (ci_out, and_1_out, and_2_out, and_3_out);
  and and_1 (and_1_out, yi, ci);
  and and_2 (and_2_out, xi, ci);
  and and_3 (and_3_out, yi, xi);
  xor xor_1 (zi, xor_2_out, ci);
  xor xor_2 (xor_2_out, xi, yi);
endmodule

module FAC (
  input  ci,
  input  xi,
  input  yi,
  output zi,
  output ci_out
);

  wire and_1_out, and_2_out, and_3_out, xor_2_out;

  or or_1 (ci_out, and_1_out, and_2_out, and_3_out);
  and and_1 (and_1_out, yi, ci);
  and and_2 (and_2_out, xi, ci);
  and and_3 (and_3_out, yi, xi);
  xor xor_1 (zi, xor_2_out, ci);
  xor xor_2 (xor_2_out, xi, yi);
endmodule
